# Fritzing sketch ar23-circuit0 (1) (saved by Fritzing 0.9.3b)
breadboards: 1

parts:
  부품1 = Arduino Uno (Rev3)
  R1 = Trimmer Potentiometer [maximum_resistance=10kΩ package=THT]

nets:
  N1: 부품1.A0, R1.wiper
  N2: 부품1.5V, R1.leg2
  N3: 부품1.GND, R1.leg1
